# Fritzing sketch StepperPCBV2 (saved by Fritzing 0.9.3b)
circuit board: 5.5cm x 5.7cm
breadboards: 1

parts:
  Raspberry_Pi_3 = Raspberry Pi 3 [part_number=RPI-3-V1.2]
  IC1 = L293D [package=THT]
  JP1 = Header 6 [package=molex-1x6_lock]

nets:
  N1: Raspberry_Pi_3.GND, IC1.0V
  N2: Raspberry_Pi_3.GPIO13, IC1.Enable_1, IC1.Enable_2
  N3: Raspberry_Pi_3.GPIO19, IC1.In_1
  N4: Raspberry_Pi_3.GPIO26, IC1.In_2
  N5: Raspberry_Pi_3.GPIO21, IC1.In_3
  N6: Raspberry_Pi_3.GPIO20, IC1.In_4
  N7: Raspberry_Pi_3.5V, IC1.+Vmotor, IC1.+V
  N8: IC1.Out_1_(_Controlled_by_Enable_1_), JP1.2
  N9: IC1.Out_2_(_Controlled_by_Enable_1_), JP1.4
  N10: IC1.Out_3_(_Controlled_by_Enable_2_), JP1.3
  N11: IC1.Out_4_(_Controlled_by_Enable_2_), JP1.1

notes:
  Bojan Lazic
  Stepper PCB V2
