# Fritzing sketch StepperGuage (saved by Fritzing 0.9.3b)
breadboards: 1

parts:
  IC1 = L293D [package=THT]
  Raspberry_Pi_1 = Raspberry Pi 3 [part_number=RPI-3-V1.2]
  M1 = Stepper Motor - Bipolar

nets:
  N1: IC1.Enable_1, IC1.Enable_2, Raspberry_Pi_1.GPIO8
  N2: IC1.In_1, Raspberry_Pi_1.GPIO24
  N3: IC1.Out_1_(_Controlled_by_Enable_1_), M1.C
  N4: IC1.0V, IC1.In_2, Raspberry_Pi_1.GND
  N5: IC1.Out_2_(_Controlled_by_Enable_1_), M1.B
  N6: IC1.+Vmotor, IC1.+V, Raspberry_Pi_1.5V
  N7: IC1.In_3, Raspberry_Pi_1.GPIO21
  N8: IC1.Out_3_(_Controlled_by_Enable_2_), M1.D
  N9: IC1.Out_4_(_Controlled_by_Enable_2_), M1.A
  N10: IC1.In_4, Raspberry_Pi_1.GPIO20

notes:
  28BYJ-48
